# Fritzing sketch reciever (saved by Fritzing 0.9.3b)
breadboards: 1

parts:
  Part1 = Arduino Cellular Shield
  Part2 = Arduino Uno (Rev3) - ICSP
  Part3 = CAN-Bus Shield
  Part4 = NRF24L01+ Breakout Board
  C1 = Capacitor Polarized [package=panasonic_d]  # not connected

nets:
  GND: Part1.GND, Part2.GND, Part3.GND, Part4.GND
  N1: Part1.RX-I, Part2.D10_PWM/SS
  N2: Part1.TX-O, Part2.D9_PWM
  N3: Part2.ICSP_MOSI, Part2.D11_PWM/MOSI, Part4.MOSI
  N4: Part2.D8, Part4.CS
  N5: Part2.D12/MISO, Part4.MISO
  N6: Part2.D13/SCK, Part4.SCK
  N7: Part2.D3_PWM, Part3.TX
  N8: Part2.D4, Part3.RX
  N9: Part2.D7, Part4.CE
  3V3: Part2.3V3, Part4.VCC
